// Logisim project projet_etu.circ as structural Verilog: 9 circuits, main circuit main
module main (
  input  Reset,
  input  ResetRAM
);

  wire Clock, Clock_out, CTRL, Exec, Fetch, getcst_1_imm, Load, ramctrl_1_memload, ramctrl_1_memstore, Store,
       WriteReg;
  wire [2:0] GetOp;
  wire [15:0] Addr, alu_1_output, getcst_1_cst, JMP_Address, MemIN, PC, R0, R1, R2, R3, R4, R5, R6, R7,
       registres_1_out_sr1, registres_1_out_sr2;
  wire [31:0] bit_extender_1_out, IR, MemOUT;

  Clock u_Clock (.out(Clock_out));
  Seq seq_1 (.ClockOrig(Clock_out), .reset(Reset), .Fetch(Fetch), .Exec(Exec), .Clock(Clock));
  LED led_1 (.in(Clock_out));
  RegPC regpc_1 (.JMP_Address(JMP_Address), .Cond(1'b0), .CTRL(CTRL), .Clock(Exec), .Reset(Reset), .PC(PC));
  // Probe on PC
  GetAddr getaddr_1 (.PC(PC), .Addr(Addr), .Fetch(Fetch), .Load(Load), .Store(Store));
  // Probe on Addr
  LED led_2 (.in(Fetch));
  LED led_3 (.in(Exec));
  // Probe on MemIN
  assign bit_extender_1_out = {{16{MemIN[15]}}, MemIN};  // Bit_Extender bit_extender_1
  // Probe on PC
  // Probe on IR
  DecodeIR decodeir_1 (
    .CTRL(CTRL), .WriteReg(WriteReg), .IR(IR), .Load(Load), .GetOp(GetOp), .JMPAddress(JMP_Address),
    .Store(Store));
  RamCtrl ramctrl_1 (
    .Store(Store), .Fetch(Fetch), .Exec(Exec), .Load(Load), .MemStore(ramctrl_1_memstore),
    .MemLoad(ramctrl_1_memload), .Clock(Clock));
  // Probe on MemOUT
  RAM #(.addrWidth(16), .dataWidth(32), .bus("separate")) ram_1 (
    .addr(Addr), .din(bit_extender_1_out), .data(MemOUT), .str(ramctrl_1_memstore), .clk(ramctrl_1_memstore),
    .ld(ramctrl_1_memload), .clr(ResetRAM));  // open: sel
  // Probe on R0
  // Probe on R3
  // Probe on R6
  Register #(.width(32), .trigger("falling")) RegIR (.D(MemOUT), .Q(IR), .clk(Fetch), .clr(Reset));  // open: en
  // Probe on R1
  // Probe on R4
  // Probe on R7
  // Probe on IR
  // Probe on R2
  // Probe on R5
  // Probe on IR[8:6]
  // Probe on IR[11:9]
  // Probe on IR[14:12]
  // Probe on getcst_1_cst
  GetCst getcst_1 (.IR(IR), .Cst(getcst_1_cst), .Imm(getcst_1_imm));
  Registres registres_1 (
    .SR1(IR[11:9]), .IN(alu_1_output), .SR2(IR[14:12]), .WriteReg(WriteReg), .DR(IR[8:6]),
    .OUT_SR1(registres_1_out_sr1), .OUT_SR2(registres_1_out_sr2), .OUT_DR(MemIN), .R0(R0), .R1(R1), .R2(R2),
    .R3(R3), .R4(R4), .R5(R5), .R6(R6), .R7(R7), .Reset(Reset), .Clock(Exec));
  // Probe on registres_1_out_sr2
  // Probe on registres_1_out_sr1
  ALU alu_1 (
    .Imm(getcst_1_imm), .e2(GetOp), .Input1(registres_1_out_sr1), .Input2(registres_1_out_sr2),
    .Cst(getcst_1_cst), .Output(alu_1_output));
  // Probe on alu_1_output
  // Probe on R0
  // Probe on R1
  // Probe on R2
  // Probe on R3
  // Probe on R4
  // Probe on R5
  // Probe on R6
  // Probe on R7
  // Probe on alu_1_output

  // Notes on the sheet:
  //   RAM
endmodule

module ALU (
  input  [15:0] Input1,
  input  [15:0] Input2,
  input  [15:0] Cst,
  input  Imm,
  input  [2:0] e2,
  output [15:0] Output
);
endmodule

module DecodeIR (
  input  [31:0] IR,
  output WriteReg,
  output Store,
  output Load,
  output CTRL,
  output [2:0] GetOp,
  output [15:0] JMPAddress
);


  assign CTRL = 1'b0;
  assign GetOp = 3'b000;
  assign JMPAddress = {16{1'b0}};
  assign Load = 1'b0;
  assign Store = 1'b0;
  assign WriteReg = 1'b1;
endmodule

module GetAddr (
  input  [15:0] PC,
  input  Load,
  input  Store,
  input  Fetch,
  output [15:0] Addr
);
endmodule

module GetCst (
  input  [31:0] IR,
  output [15:0] Cst,
  output Imm
);

  Bit_Extender #(.in_width(20)) bit_extender_1 (.in(IR[31:12]), .out(Cst));

  assign Imm = IR[5];
endmodule

module RamCtrl (
  input  Clock,
  input  Exec,
  input  Fetch,
  input  Load,
  input  Store,
  output MemLoad,
  output MemStore
);

  wire and_1_out;

  and and_1 (and_1_out, Exec, Load);
  and and_2 (MemStore, Exec, Clock, Store);
  or or_1 (MemLoad, Fetch, and_1_out);
endmodule

module Registres (
  input  [15:0] IN,
  input  [2:0] SR1,
  input  [2:0] SR2,
  input  [2:0] DR,
  input  WriteReg,
  input  Clock,
  input  Reset,
  output [15:0] R0,
  output [15:0] OUT_SR1,
  output [15:0] R1,
  output [15:0] R2,
  output [15:0] R3,
  output [15:0] OUT_SR2,
  output [15:0] R4,
  output [15:0] R5,
  output [15:0] OUT_DR,
  output [15:0] R6,
  output [15:0] R7
);

  wire [15:0] and_1_out, and_3_out, and_5_out, and_7_out, and_9_out, SR1R0, SR1R1, SR1R2, SR1R3, SR1R4,
       SR1R5, SR1R6, SR1R7, SR2R0, SR2R1, SR2R2, SR2R3, SR2R4, SR2R5, SR2R6, SR2R7, undriven, undriven_2,
       undriven_3, undriven_4, undriven_5, undriven_6, undriven_7, undriven_8;

  Multiplexer #(.select(3), .width(16)) multiplexer_1 (
    .in0(SR1R0), .in1(SR1R1), .in2(SR1R2), .in3(SR1R3), .in4(SR1R4), .in5(SR1R5), .in6(SR1R6), .in7(SR1R7),
    .sel(SR1));  // open: out, en
  Multiplexer #(.select(3), .width(16)) multiplexer_2 (
    .in0(SR2R0), .in1(SR2R1), .in2(SR2R2), .in3(SR2R3), .in4(SR2R4), .in5(SR2R5), .in6(SR2R6), .in7(SR2R7),
    .sel(SR2));  // open: out, en
  Register #(.width(16), .trigger("falling")) u_R0 (.Q(R0), .clk(Clock), .clr(Reset));  // open: D, en
  Register #(.width(16), .trigger("falling")) u_R1 (.Q(R1), .clk(Clock), .clr(Reset));  // open: D, en
  Register #(.width(16), .trigger("falling")) u_R2 (.Q(R2), .clk(Clock), .clr(Reset));  // open: D, en
  Register #(.width(16), .trigger("falling")) u_R3 (.Q(R3), .clk(Clock), .clr(Reset));  // open: D, en
  Register #(.width(16), .trigger("falling")) u_R4 (.Q(R4), .clk(Clock), .clr(Reset));  // open: D, en
  Register #(.width(16), .trigger("falling")) u_R5 (.Q(R5), .clk(Clock), .clr(Reset));  // open: D, en
  Register #(.width(16), .trigger("falling")) u_R6 (.Q(R6), .clk(Clock), .clr(Reset));  // open: D, en
  Register #(.width(16), .trigger("falling")) u_R7 (.Q(R7), .clk(Clock), .clr(Reset));  // open: D, en
  assign and_1_out = SR1R0 & undriven;  // AND_Gate and_1, 16 bits wide
  // AND_Gate and_2 has open pins: in0=undriven, out=open
  assign and_3_out = undriven_2;  // AND_Gate and_3, 16 bits wide AND_Gate
  // AND_Gate and_4 has open pins: in0=undriven_2, out=open
  assign and_5_out = undriven_6;  // AND_Gate and_5, 16 bits wide AND_Gate
  // AND_Gate and_6 has open pins: in0=undriven_6, out=open
  assign and_7_out = undriven_7;  // AND_Gate and_7, 16 bits wide AND_Gate
  // AND_Gate and_8 has open pins: in0=undriven_7, out=open
  assign and_9_out = undriven_3;  // AND_Gate and_9, 16 bits wide AND_Gate
  // AND_Gate and_10 has open pins: in0=undriven_3, out=open
  // AND_Gate and_11 has open pins: in1=undriven_4, out=open
  // AND_Gate and_12 has open pins: in0=undriven_4, out=open
  // AND_Gate and_13 has open pins: in1=undriven_5, out=open
  // AND_Gate and_14 has open pins: in0=undriven_5, out=open
  // AND_Gate and_15 has open pins: in1=undriven_8, out=open
  // AND_Gate and_16 has open pins: in0=undriven_8, out=open
  assign OUT_SR1 = and_1_out | and_3_out | and_5_out | and_7_out | and_9_out;  // OR_Gate or_1, 16 bits wide
  // OR_Gate or_2 has open pins: out=OUT_SR2
endmodule

module RegPC (
  input  [15:0] JMP_Address,
  input  Cond,
  input  CTRL,
  input  Clock,
  input  Reset,
  output [15:0] PC
);

  Register #(.width(16), .trigger("falling")) u_PC (.Q(PC), .clk(Clock), .clr(Reset));  // open: D, en
endmodule

module Seq (
  input  ClockOrig,
  input  reset,
  output Fetch,
  output Exec,
  output Clock
);

  Register #(.width(1), .trigger("falling")) register_1 (
    .D(Fetch), .Q(Exec), .clk(ClockOrig), .clr(reset));  // open: en
  not not_1 (Fetch, Exec);
  buf buffer_1 (Clock, ClockOrig);
endmodule
